# Fritzing sketch Smart-Farm-SystemFRITZ (saved by Fritzing 0.9.4)
breadboards: 3

parts:
  Breadboard4 = Breadboard Split Power
  Breadboard5 = Breadboard Split Power
  Argon1 = Particle Argon
  Grove1 = Grove Dust Sensor
  SENS1 = SoilWatch 10
  M1 = BMP280
  OLED_I2C1 = OLED 128x64 I2C Monochrome Display
  MOTOR1 = 28BYJ-48 Stepper Motor
  X1 = X113647 Stepper Driver Board [part_number=X113647 package=board]
  HC-SR04_Sensor_1 = HC-SR04 Ultrasonic Distance Sensor
  GY1 = MPU-6050 Board GY-521 [form="♀ (female)" package=THT]

nets:
  VCC: Breadboard4.pin15Y, Breadboard4.pin17Y, Breadboard4.pin21Y, Breadboard4.pin29Y, Breadboard5.pin3Y, Breadboard5.pin15Y, Breadboard5.pin17Y, Breadboard5.pin26Y, Breadboard5.pin29Y, Argon1.3.3V, Grove1.VCC, SENS1.VCC, M1.VIN, OLED_I2C1.VDD, GY1.pin1
  GND: Breadboard4.pin20Z, Breadboard4.pin29Z, Breadboard5.pin3Z, Breadboard5.pin25Z, Breadboard5.pin29Z, Argon1.GND, Grove1.GND, SENS1.GND, M1.GND, OLED_I2C1.GND, X1.GND, GY1.pin2
  N1: Argon1.A0, Grove1.SIG
  N2: Argon1.A1, SENS1.OUT
  N3: Argon1.SDA, M1.SDA, OLED_I2C1.SDA, GY1.pin4
  N4: Argon1.SCL, M1.SCL, OLED_I2C1.SCK, GY1.pin3
  N5: Argon1.D2, X1.IN4
  N6: Argon1.D3, X1.IN3
  N7: Argon1.D4, X1.IN2
  N8: Argon1.D5, X1.IN1
  N9: Argon1.D6, HC-SR04_Sensor_1.ECHO
  N10: Argon1.D7, Argon1.D8, HC-SR04_Sensor_1.TRIG
  N11: Argon1.VUSB, X1.+V, HC-SR04_Sensor_1.VCC
  N12: MOTOR1.BLUE, X1.BLUE
  N13: MOTOR1.PINK, X1.PINK
  N14: MOTOR1.RED, X1.RED
  N15: MOTOR1.ORANGE, X1.ORANGE
  N16: MOTOR1.YELLOW, X1.YELLOW

custom parts:
  Breadboard Split Power: A custom 6 pin per group power supply strip where the top row (ground) is all bussed together and the bottom row (+V) is split in two groups of 12 pins. This version is modified to be a loadable part and was rescaled to be on the standard 1px = 1thou grid with the size set in inches
  Particle Argon: The Argon is a powerful Wi-Fi enabled development board that can act as either a standalone Wi-Fi endpoint or Wi-Fi enabled gateway for Particle Mesh networks. It is based on the Nordic nRF52840 and has built-in battery charging circuitry so it’s easy to connect a Li-Po and deploy your local network in minutes. The Argon is great for connecting existing projects to the Particle Device Cloud or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
  Grove Dust Sensor: PPD42 Grove Dust Sensor
  SoilWatch 10: SoilWatch 10 - Capacitive soil moisture sensor
  BMP280: Temperature Humidity Barometric presure Sensor, I2C
  28BYJ-48 Stepper Motor: 28BYJ-48 gear-reduction stepper motor (small)
  X113647 Stepper Driver Board: A common stepper motor driver board based on ULN2003APG darlington array
  MPU-6050 Board GY-521: Acelerometro y Giroscopio MPU-6050 Board GY-521
